# Fritzing sketch servomoteur_fritzing (saved by Fritzing 0.4.2b)
breadboards: 1

parts:
  J1 = Basic Servo
  R1 = Rotary Potentiometer (Large) [package=THT]
  Arduino2 = Arduino

nets:
  GND: J1.gnd, R1.leg2, Arduino2.GND
  VCC: J1.vcc, R1.leg1, Arduino2.+5V
  N1: J1.pulse, Arduino2.D9
  N2: R1.wiper, Arduino2.A2

notes:
  Dans cet exemple, la position du potentiometre est lue par une entrée analogique, puis transmise au servomoteur pour piloter sa position. voir aussi: http://arduino.cc/en/Tutorial/AnalogInput http://arduino.cc/en/Tutorial/Knob
