# Fritzing sketch contact (saved by Fritzing 0.4.2b)
breadboards: 1

parts:
  Arduino1 = Arduino
  R1 = Resistor [resistance=220 package=THT]
  S1 = Pushbutton [package="[THT]"]

nets:
  N1: Arduino1.GND, R1.Pin_1
  N2: Arduino1.D4, Arduino1.+5V, R1.Pin_0, S1.Pin_1, S1.Pin_2, S1.Pin_3, S1.Pin_4

notes:
  La resistance est là pour limiter la consomation quand ll'interrupteur est fermé
  [ARDUINO]
  utiliser un interrupteur
