# Fritzing sketch contact (saved by Fritzing 0.3.14b)
breadboards: 1

parts:
  Arduino1 = Arduino
  R1 = Resistor [resistance=220 package=THT]

nets:
  N1: Arduino1.GND, R1.Pin_1
  N2: Arduino1.D2, R1.Pin_0
